// Logisim project LE_Lab2.circ as structural Verilog: 3 circuits, main circuit main
module main (
  input  A1,
  input  B1,
  input  C1,
  input  A2,
  input  B2,
  input  C2,
  input  D2,
  output True1,
  output True2
);

  Equation_1 equation_1_1 (.In1A(A1), .In1B(B1), .In1C(C1), .Out1(True1));
  Equation_2 equation_2_1 (.In2A(A2), .In2B(B2), .In2C(C2), .In2D(D2), .Out2(True2));

  // Notes on the sheet:
  //   Aitbayev Aslanbek
  //   Lab 02: Boolean Equations
  //   December 12, 2024
endmodule

module Equation_1 (
  input  In1A,
  input  In1B,
  input  In1C,
  output Out1
);

  wire and_1_out, and_2_out, and_3_out, not_1_out, not_2_out, not_3_out, not_4_out;

  not not_1 (not_1_out, In1A);
  and and_1 (and_1_out, not_1_out, In1B, not_2_out);
  not not_2 (not_2_out, In1C);
  not not_3 (not_3_out, In1B);
  and and_2 (and_2_out, In1A, not_3_out, not_4_out);
  not not_4 (not_4_out, In1C);
  and and_3 (and_3_out, In1A, In1B, In1C);
  or or_1 (Out1, and_1_out, and_2_out, and_3_out);

  // Notes on the sheet:
  //   (A'BC')+(AB'C')+(ABC)
endmodule

module Equation_2 (
  input  In2A,
  input  In2B,
  input  In2C,
  input  In2D,
  output Out2
);

  wire and_1_out, and_2_out, and_3_out, and_4_out, not_1_out, not_2_out, not_3_out, not_4_out, not_5_out,
       not_6_out, not_7_out;

  not not_1 (not_1_out, In2A);
  not not_2 (not_2_out, In2B);
  and and_1 (and_1_out, not_1_out, not_2_out, In2C, not_3_out);
  not not_3 (not_3_out, In2D);
  not not_4 (not_4_out, In2A);
  and and_2 (and_2_out, not_4_out, In2B, In2C, In2D);
  not not_5 (not_5_out, In2B);
  and and_3 (and_3_out, In2A, not_5_out, In2C, not_6_out);
  not not_6 (not_6_out, In2D);
  and and_4 (and_4_out, In2A, In2B, In2C, not_7_out);
  not not_7 (not_7_out, In2D);
  or or_1 (Out2, and_1_out, and_2_out, and_3_out, and_4_out);

  // Notes on the sheet:
  //   (A'B'CD')+(A'BCD)+(AB'CD')+(ABCD')
endmodule
