// Logisim project LE_Lab3.circ as structural Verilog: 2 circuits, main circuit main
module main (
  input  In1,
  input  In2,
  input  In3,
  input  In4,
  input  In5,
  input  In6,
  input  In7,
  input  In8,
  input  In9,
  output [3:0] out_10
);

  Encoder encoder_1 (
    .In1(In1), .In2(In2), .In3(In3), .In4(In4), .In5(In5), .In6(In6), .In7(In7), .In8(In8), .In9(In9),
    .Out1(out_10[0]), .Out2(out_10[1]), .Out3(out_10[2]), .Out4(out_10[3]));
  Hex_Digit_Display hex_digit_display_1 (.value(out_10));  // open: dp

  // Notes on the sheet:
  //   Aitbayev Aslanbek
  //   Lab 03: Nine-Line Priority Encoder
  //   December 13, 2024
endmodule

module Encoder (
  input  In1,
  input  In2,
  input  In3,
  input  In4,
  input  In5,
  input  In6,
  input  In7,
  input  In8,
  input  In9,
  output Out1,
  output Out2,
  output Out3,
  output Out4
);

  wire not_1_out, not_2_out, not_3_out, not_4_out, not_5_out, not_6_out, not_7_out, not_8_out, not_9_out,
       not_10_out, not_11_out, U1_out, U2_out, U3_out, U4_out, U5_out, U6_out, U7_out, U8_out, U9_out,
       U10_out, U11_out, U12_out, U16_out;

  or U16 (U16_out, In8, In9);
  not not_1 (not_1_out, U16_out);
  not not_2 (not_2_out, In2);
  not not_3 (not_3_out, In4);
  not not_4 (not_4_out, In6);
  not not_5 (not_5_out, In4);
  not not_6 (not_6_out, In6);
  not not_7 (not_7_out, In6);
  not not_8 (not_8_out, In4);
  not not_9 (not_9_out, In7);
  not not_10 (not_10_out, In4);
  not not_11 (not_11_out, In7);
  and U1 (U1_out, In1, not_2_out, not_3_out, not_4_out, not_1_out);
  and U2 (U2_out, In3, not_5_out, not_6_out, not_1_out);
  and U3 (U3_out, In5, not_7_out, not_1_out);
  and U4 (U4_out, In7, not_1_out);
  and U5 (U5_out, In2, not_8_out, not_9_out, not_1_out);
  and U6 (U6_out, not_10_out, not_11_out, In3, not_1_out);
  and U7 (U7_out, In6, not_1_out);
  and U8 (U8_out, In7, not_1_out);
  and U9 (U9_out, In4, not_1_out);
  and U10 (U10_out, In5, not_1_out);
  and U11 (U11_out, In6, not_1_out);
  and U12 (U12_out, In7, not_1_out);
  or U13 (Out1, U1_out, U2_out, U3_out, U4_out, In9);
  or U14 (Out2, U5_out, U6_out, U7_out, U8_out);
  or U15 (Out3, U9_out, U10_out, U11_out, U12_out);
  or U17 (Out4, In9, In8);
endmodule
