// Logisim project LE_Lab4.circ as structural Verilog: 4 circuits, main circuit main
module main (
  input  Cln,
  input  [3:0] InA,
  input  [3:0] InB,
  input  [2:0] Sel,
  input  Mode,
  output Cout,
  output Cmp,
  output [3:0] ALUOut
);

  ALU alu_1 (.Cln(Cln), .InA(InA), .InB(InB), .Sel(Sel), .Mode(Mode), .Cout(Cout), .Cmp(Cmp), .ALUout(ALUOut));

  // Notes on the sheet:
  //   Aitbayev Aslanbek
  //   Lab 04: ALU
  //   December 13, 2024
endmodule

module ALU (
  input  Cln,
  input  [3:0] InA,
  input  [3:0] InB,
  input  [2:0] Sel,
  input  Mode,
  output Cout,
  output Cmp,
  output [3:0] ALUout
);

  wire [3:0] arithmetic_1_arout, logic_1_loout;

  Arithmetic arithmetic_1 (
    .Cln(Cln), .InA(InA), .InB(InB), .Sel(Sel), .Arout(arithmetic_1_arout), .Cout(Cout), .Cmp(Cmp));
  Logic logic_1 (.InA(InA), .InB(InB), .Sel(Sel), .LoOut(logic_1_loout));
  Multiplexer #(.width(4)) multiplexer_1 (.in0(arithmetic_1_arout), .in1(logic_1_loout), .out(ALUout), .sel(Mode));
endmodule

module Arithmetic (
  input  Cln,
  input  [3:0] InA,
  input  [3:0] InB,
  input  [2:0] Sel,
  output [3:0] Arout,
  output Cout,
  output Cmp
);

  wire adder_1_cout, adder_2_cout, adder_3_cout, subtractor_1_bout, subtractor_2_bout, subtractor_3_bout,
       subtractor_4_bout;
  wire [3:0] adder_1_out, adder_2_out, adder_3_out, multiplier_1_out, multiplier_2_out, not_1_out, not_2_out,
       subtractor_1_out, subtractor_2_out, subtractor_3_out, subtractor_4_out;

  Subtractor #(.width(4)) subtractor_1 (
    .a(InA), .b(4'b0001), .out(subtractor_1_out), .bin(Cln), .bout(subtractor_1_bout));
  Adder #(.width(4)) adder_1 (.a(InA), .b(InB), .out(adder_1_out), .cin(Cln), .cout(adder_1_cout));
  Subtractor #(.width(4)) subtractor_2 (.a(InA), .b(InB), .out(subtractor_2_out), .bin(Cln), .bout(subtractor_2_bout));
  Multiplier #(.width(4)) multiplier_1 (.a(InA), .b(InB), .out(multiplier_1_out));  // open: cin, cout
  Multiplier #(.width(4)) multiplier_2 (.a(InA), .b(not_1_out), .out(multiplier_2_out));  // open: cin, cout
  assign not_1_out = ~InB;  // NOT_Gate not_1, 4 bits wide
  Adder #(.width(4)) adder_2 (.a(InA), .b(InA), .out(adder_2_out), .cin(Cln), .cout(adder_2_cout));
  Adder #(.width(4)) adder_3 (.a(InA), .b(4'b0001), .out(adder_3_out), .cin(Cln), .cout(adder_3_cout));
  Comparator #(.width(4)) comparator_1 (.a(InA), .b(InB), .eq(Cmp));  // open: gt, lt
  Subtractor #(.width(4)) subtractor_3 (
    .a(multiplier_1_out), .b(4'b0001), .out(subtractor_3_out), .bout(subtractor_3_bout));  // open: bin
  Subtractor #(.width(4)) subtractor_4 (
    .a(multiplier_2_out), .b(4'b0001), .out(subtractor_4_out), .bout(subtractor_4_bout));  // open: bin
  assign not_2_out = ~4'b0001;  // NOT_Gate not_2, 4 bits wide
  Multiplexer #(.select(3), .width(4)) multiplexer_1 (
    .in0(not_2_out), .in1(subtractor_1_out), .in2(adder_1_out), .in3(subtractor_2_out),
    .in4(subtractor_3_out), .in5(subtractor_4_out), .in6(adder_2_out), .in7(adder_3_out), .out(Arout),
    .sel(Sel));
  Multiplexer #(.select(3)) multiplexer_2 (
    .in0(1'b0), .in1(subtractor_1_bout), .in2(adder_1_cout), .in3(subtractor_2_bout),
    .in4(subtractor_3_bout), .in5(subtractor_4_bout), .in6(adder_2_cout), .in7(adder_3_cout), .out(Cout),
    .sel(Sel));
endmodule

module Logic (
  input  [3:0] InA,
  input  [3:0] InB,
  input  [2:0] Sel,
  output [3:0] LoOut
);

  wire [3:0] AB_out, and_1_out, and_2_out, not_1_out, not_2_out, not_3_out, not_4_out, not_5_out, or_1_out,
       or_2_out, or_3_out, xor_1_out;

  assign not_1_out = ~InB;  // NOT_Gate not_1, 4 bits wide
  assign not_2_out = ~InB;  // NOT_Gate not_2, 4 bits wide
  assign AB_out = InA & InB;  // AND_Gate AB, 4 bits wide
  assign and_1_out = InA & InB;  // AND_Gate and_1, 4 bits wide
  assign or_1_out = InA | InB;  // OR_Gate or_1, 4 bits wide
  assign or_2_out = InA | InB;  // OR_Gate or_2, 4 bits wide
  assign xor_1_out = InA ^ InB;  // XOR_Gate xor_1, 4 bits wide
  assign and_2_out = InA & not_1_out;  // AND_Gate and_2, 4 bits wide
  assign or_3_out = InA | not_2_out;  // OR_Gate or_3, 4 bits wide
  assign not_3_out = ~and_1_out;  // NOT_Gate not_3, 4 bits wide
  assign not_4_out = ~or_2_out;  // NOT_Gate not_4, 4 bits wide
  assign not_5_out = ~InA;  // NOT_Gate not_5, 4 bits wide
  Multiplexer #(.select(3), .width(4)) multiplexer_1 (
    .in0(AB_out), .in1(not_3_out), .in2(or_1_out), .in3(not_4_out), .in4(xor_1_out), .in5(and_2_out),
    .in6(or_3_out), .in7(not_5_out), .out(LoOut), .sel(Sel));

  // Notes on the sheet:
  //   0=AB
  //   5=AB'
  //   7=A'
  //   1=(AB)'
  //   2=A+B
  //   3=(A+B)'
  //   4=A Xor B
  //   6=A+B'
endmodule
