// Logisim project LE_Lab5.circ as structural Verilog: 6 circuits, main circuit main
module main (
  input  clk,
  input  rst,
  output [3:0] out_3,
  output [3:0] out_4,
  output [3:0] out_5,
  output [3:0] out_6,
  output [3:0] out_7
);

  assUp assup_1 (.clk(clk), .rst(rst), .Up(out_3));
  assDown assdown_1 (.clk(clk), .rst(rst), .Up(out_4));
  assDecade assdecade_1 (.clk(clk), .rst(rst), .Up(out_5));
  ssRing ssring_1 (.clk(clk), .rst(rst), .Up(out_6));
  ssJohnson ssjohnson_1 (.clk(clk), .rst(rst), .Up(out_7));
  Hex_Digit_Display hex_digit_display_1 (.value(out_3));  // open: dp
  Hex_Digit_Display hex_digit_display_2 (.value(out_4));  // open: dp
  Hex_Digit_Display hex_digit_display_3 (.value(out_5));  // open: dp
  Hex_Digit_Display hex_digit_display_4 (.value(out_6));  // open: dp
  Hex_Digit_Display hex_digit_display_5 (.value(out_7));  // open: dp

  // Notes on the sheet:
  //   Lab 05: Counters
  //   December 13, 2024
  //   Aitbayev Aslanbek
endmodule

module assUp (
  input  clk,
  input  rst,
  output [3:0] Up
);

  wire d_ff_1_qn, d_ff_2_qn, d_ff_3_qn, d_ff_4_qn;

  D_Flip_Flop d_ff_1 (.D(d_ff_1_qn), .clk(clk), .Q(Up[0]), .Qn(d_ff_1_qn), .reset(rst));  // open: preset
  D_Flip_Flop d_ff_2 (.D(d_ff_2_qn), .clk(d_ff_1_qn), .Q(Up[1]), .Qn(d_ff_2_qn), .reset(rst));  // open: preset
  D_Flip_Flop d_ff_3 (.D(d_ff_3_qn), .clk(d_ff_2_qn), .Q(Up[2]), .Qn(d_ff_3_qn), .reset(rst));  // open: preset
  D_Flip_Flop d_ff_4 (.D(d_ff_4_qn), .clk(d_ff_3_qn), .Q(Up[3]), .Qn(d_ff_4_qn), .reset(rst));  // open: preset
endmodule

module assDown (
  input  clk,
  input  rst,
  output [3:0] Up
);

  wire d_ff_1_qn, d_ff_2_qn, d_ff_3_qn, d_ff_4_qn;

  D_Flip_Flop d_ff_1 (.D(d_ff_1_qn), .clk(clk), .Q(Up[0]), .Qn(d_ff_1_qn), .preset(rst));  // open: reset
  D_Flip_Flop d_ff_2 (.D(d_ff_2_qn), .clk(Up[0]), .Q(Up[1]), .Qn(d_ff_2_qn), .preset(rst));  // open: reset
  D_Flip_Flop d_ff_3 (.D(d_ff_3_qn), .clk(Up[1]), .Q(Up[2]), .Qn(d_ff_3_qn), .preset(rst));  // open: reset
  D_Flip_Flop d_ff_4 (.D(d_ff_4_qn), .clk(Up[2]), .Q(Up[3]), .Qn(d_ff_4_qn), .preset(rst));  // open: reset
endmodule

module assDecade (
  input  clk,
  input  rst,
  output [3:0] Up
);

  wire and_1_out, d_ff_1_qn, d_ff_2_qn, d_ff_3_qn, d_ff_4_qn, or_1_out;

  or or_1 (or_1_out, rst, and_1_out);
  D_Flip_Flop d_ff_1 (.D(d_ff_1_qn), .clk(clk), .Q(Up[0]), .Qn(d_ff_1_qn), .reset(or_1_out));  // open: preset
  D_Flip_Flop d_ff_2 (.D(d_ff_2_qn), .clk(d_ff_1_qn), .Q(Up[1]), .Qn(d_ff_2_qn), .reset(or_1_out));  // open: preset
  Hex_Digit_Display hex_digit_display_1 (.value(Up));  // open: dp
  D_Flip_Flop d_ff_3 (.D(d_ff_3_qn), .clk(d_ff_2_qn), .Q(Up[2]), .Qn(d_ff_3_qn), .reset(or_1_out));  // open: preset
  D_Flip_Flop d_ff_4 (.D(d_ff_4_qn), .clk(d_ff_3_qn), .Q(Up[3]), .Qn(d_ff_4_qn), .reset(or_1_out));  // open: preset
  and and_1 (and_1_out, Up[3], Up[1]);
endmodule

module ssRing (
  input  clk,
  input  rst,
  output [3:0] Up
);

  D_Flip_Flop d_ff_1 (.D(Up[3]), .clk(clk), .Q(Up[0]), .preset(rst));  // open: Qn, reset
  D_Flip_Flop d_ff_2 (.D(Up[0]), .clk(clk), .Q(Up[1]), .reset(rst));  // open: Qn, preset
  D_Flip_Flop d_ff_3 (.D(Up[1]), .clk(clk), .Q(Up[2]), .reset(rst));  // open: Qn, preset
  D_Flip_Flop d_ff_4 (.D(Up[2]), .clk(clk), .Q(Up[3]), .reset(rst));  // open: Qn, preset
endmodule

module ssJohnson (
  input  clk,
  input  rst,
  output [3:0] Up
);

  wire d_ff_4_qn;

  D_Flip_Flop d_ff_1 (.D(d_ff_4_qn), .clk(clk), .Q(Up[0]), .preset(rst));  // open: Qn, reset
  D_Flip_Flop d_ff_2 (.D(Up[0]), .clk(clk), .Q(Up[1]), .reset(rst));  // open: Qn, preset
  D_Flip_Flop d_ff_3 (.D(Up[1]), .clk(clk), .Q(Up[2]), .reset(rst));  // open: Qn, preset
  D_Flip_Flop d_ff_4 (.D(Up[2]), .clk(clk), .Q(Up[3]), .Qn(d_ff_4_qn), .reset(rst));  // open: preset
endmodule
